# Fritzing sketch fr (saved by Fritzing 0.9.3b)
breadboards: 1

parts:
  Часть1 = Arduino Pro Mini v13
  Q1 = Basic FET P-Channel [package="TO220 [THT]"]
  R1 = Resistor [tolerance=±5% resistance=4.7k package=THT]
  LCD1 = LCD screen
  R3 = Trimmer Potentiometer [maximum_resistance=1kΩ package=THT]
  BAT1 = Battery Holders [package=battery-aa-kit]
  oil_pump = Vibration Motor- ROB-08449 [package=vibe-motor-10mm]
  RE1 = Water flow meter
  RE2 = Water flow meter

nets:
  VCC: Часть1.VCC, LCD1.VDD
  GND: Часть1.GND, Q1.source, LCD1.VSS, LCD1.R/W, R3.leg2, BAT1.-, RE1.WaterFlowMeterPinC, RE2.WaterFlowMeterPinC
  N1: Часть1.RAW, BAT1.+, oil_pump.+, RE1.WaterFlowMeterPinB, RE2.WaterFlowMeterPinB
  N2: Часть1.D10_PWM/SS, R1.Pin_0
  N3: Часть1.D9_PWM, LCD1.DB7
  N4: Часть1.D8, LCD1.DB6
  N5: Часть1.D7, LCD1.DB5
  N6: Часть1.D6_PWM, LCD1.DB4
  N7: Часть1.D5_PWM, LCD1.E
  N8: Часть1.D4, LCD1.RS
  N9: Часть1.D3_PWM, RE1.WaterFlowMeterPinA
  N10: Часть1.D2, RE2.WaterFlowMeterPinA
  N11: Q1.gate, R1.Pin_1
  N12: Q1.drain, oil_pump.-
  N13: LCD1.V0, R3.wiper

// code stored in the sketch: maslo.ino
#include <Wire.h>
#include <LiquidCrystal.h>
LiquidCrystal lcd(4, 5, 6, 7, 8, 9);  

const float calibrationFactor = 4.5; //?????????? ????????? 4.5 = 450 ?????????/????
const byte StartPWM = 60;            //??????????? ??? ??????? ?????? 0-255
const int Tik = 100;                 //???????? ?????????? ?????? ? ????????? ? ??.
volatile byte pulseCount1;  
volatile byte pulseCount2;  
unsigned long TotalMl1;
unsigned long TotalMl2;
unsigned long oldTime;
unsigned long CurMillis;

//??? floatToString
char charBuf[8]; 
static byte addon_letters[16];

void init_rus(const char* letters_use ){ // ????????? ? ??????? ??????? ??????? ?????
  // ? ???????? ????????? ????? ???????????? ?????: "?????????????????????"
  // ?? 16 ????, ?? ????????????? ?? ????? 8
  // ??????? ????
  static byte letters[][8]   = {
    { B11111, B10000, B10000, B11111, B10001, B10001, B11111, B00000 },//?
    { B11111, B10000, B10000, B10000, B10000, B10000, B10000, B00000 },//?
    { B01111, B01001, B01001, B01001, B01001, B11111, B10001, B00000 },//?
    { B10101, B10101, B10101, B01110, B10101, B10101, B10101, B00000 },//?
    { B01110, B10001, B00001, B00110, B00001, B10001, B01110, B00000 },//?
    { B10001, B10001, B10011, B10101, B11001, B10001, B10001, B00000 },//?
    { B10101, B10101, B10011, B10101, B11001, B10001, B10001, B00000 },//?
    { B00111, B01001, B10001, B10001, B10001, B10001, B10001, B00000 },//?
    { B11111, B10001, B10001, B10001, B10001, B10001, B10001, B00000 },//?
    { B10001, B10001, B10001, B01111, B00001, B10001, B01110, B00000 },//?
    { B01110, B10101, B10101, B10101, B01110, B00100, B00100, B00000 },//?
    { B10001, B10001, B10001, B10001, B10001, B10001, B11111, B00001 },//?
    { B10001, B10001, B10001, B01111, B00001, B00001, B00001, B00000 },//?
    { B10101, B10101, B10101, B10101, B10101, B10101, B11111, B00000 },//?
    { B10101, B10101, B10101, B10101, B10101, B10101, B11111, B00001 },//?
    { B10000, B10000, B10000, B11110, B10001, B10001, B11110, B00000 },//?
    { B11000, B01000, B01110, B01001, B01001, B01001, B01110, B00000 },//?
    { B10001, B10001, B10001, B11101, B10101, B10101, B11101, B00000 },//?
    { B11110, B00001, B00001, B01111, B00001, B00001, B11110, B00000 },//?
    { B10111, B10101, B10101, B11101, B10101, B10101, B10111, B00000 },//?
    { B01111, B10001, B10001, B01111, B10001, B10001, B10001, B00000 },//?
  };
  static char chars[] = {'?', '?', '?', '?', '?', '?', '?', '?', '?', '?', '?', '?', '?', '?', '?', '?', '?', '?', '?', '?', '?'};
  static byte empty[8] = { 0, 0, 0, 0, 0, 0, 0, 0 };
  int index = 0, cl = sizeof(chars) / sizeof(char), i, j, symb;
  memset(addon_letters, 0, sizeof(addon_letters));
  for ( j = 0; j < (int)strlen(letters_use) && j < 16; j++ )
    lcd.createChar(j, empty);

  for ( j = 0; j < (int)strlen(letters_use) && j < 16; j++ )
  {
    symb = -1;
    for ( i = 0; i < cl; i++ ) if ( chars[i] == letters_use[j] ) {
        symb = i;
        addon_letters[index] = letters_use[j];
        break;
      }
    if ( symb != -1 ) {
      lcd.createChar(index, letters[symb]);
      index++;
    }
  }
}

void print_rus(char *str) {  // ?????? ?? LCD ???????? ??????? ? ??????????? ???????? ?? ????????
  static char rus_letters[] = {'?', '?', '?', '?', '?', '?', '?', '?', '?', '?', '?', '?'};
  static char trans_letters[] = {'A', 'B', 'E', 'E', 'K', 'M', 'H', 'O', 'P', 'C', 'T', 'X'};
  int lcount = sizeof(rus_letters) / sizeof(char), i, j;
  for ( i = 0; i < (int)strlen(str); i++ )
  {
    if ( byte(str[i]) == 208 ) continue; // 208 ??????????
    int found = 0;
    for (j = 0; j < 16; j++) if ( addon_letters[j] != 0 && byte(str[i]) == byte(addon_letters[j]) ) {
        lcd.write(j);
        found = 1;
        break;
      }
    if (!found) for (j = 0; j < lcount; j++) if ( byte(str[i]) == byte(rus_letters[j]) ) {
          lcd.write(trans_letters[j]);
          found = 1;
          break;
        }
    if (!found) lcd.write(byte(str[i]));
  }
}

void print_rus(int x, int y, char *str) { // ?????? ?? LCD ???????? ??????? ?? ????????? ???????????
  lcd.setCursor(x, y);
  print_rus(str);
}

char * floatToString(char * outstr, double val, byte precision, byte widthp){ //????? ??? ?????????, ?????, ???????? (????? ???????), ??????????? ?????
  char temp[16];
  byte i;

  //?????? ?????????? 
  double roundingFactor = 0.5;
  unsigned long mult = 1;
  for (i = 0; i < precision; i++)
  {
    roundingFactor /= 10.0;
    mult *= 10;
  }
  
  temp[0]='\0';
  outstr[0]='\0';

  if(val < 0.0){
    strcpy(outstr,"-\0");
    val = -val;
  }

  val += roundingFactor;

  strcat(outstr, itoa(int(val),temp,10));  // ????? ?????
  if( precision > 0) {
    strcat(outstr, ".\0"); // ???????
    unsigned long frac;
    unsigned long mult = 1;
    byte padding = precision -1;
    while(precision--)
      mult *=10;

    if(val >= 0)
      frac = (val - int(val)) * mult;
    else
      frac = (int(val)- val ) * mult;
    unsigned long frac1 = frac;

    while(frac1 /= 10)
      padding--;

    while(padding--)
      strcat(outstr,"0\0");

    strcat(outstr,itoa(frac,temp,10));
  }
  
  return outstr;
}

void setup(){

  lcd.begin(16, 2); 
  init_rus("????");                     // ????????? ????? ?? 16 ????? ?? 8
  //               12345678901234567890
  
  print_rus(0, 0, (char*)"?????: ");
  print_rus(0, 1, (char*)"?????: ");
   
  pinMode(2, INPUT);
  pinMode(3, INPUT);
  digitalWrite(2,HIGH);
  digitalWrite(3,HIGH);

  pinMode(10, OUTPUT);
  pinMode(13, OUTPUT);
  attachInterrupt(0, pulseCounter1, FALLING); // ??? D2
  attachInterrupt(1, pulseCounter2, FALLING); // ??? D3
}

void loop(){
   if((millis() - oldTime) > Tik)
  { 
    CurMillis = millis() - oldTime;
    oldTime = millis();
    TotalMl1 += 1000 / CurMillis * pulseCount1 / calibrationFactor / 60 * Tik;
    TotalMl2 += 1000 / CurMillis * pulseCount2 / calibrationFactor / 60 * Tik;
    pulseCount1 = 0;
    pulseCount2 = 0;

    print_rus(7, 0, floatToString(charBuf,TotalMl1,0,8));
    print_rus(7, 1, floatToString(charBuf,TotalMl2,0,8));
    if (TotalMl1 > TotalMl2) {
        digitalWrite(13,HIGH);
        int razn = TotalMl1 - TotalMl2;
        int intens = min(razn + StartPWM,255);
        //print_rus(11, 0, left(strcat(razn,"    ")),5);
        print_rus(12, 1, strcat(floatToString(charBuf,intens/2.55,0,3),"%  "));
        analogWrite(10,intens);
      } else {
        digitalWrite(13,LOW);
        analogWrite(10,0);
        print_rus(12, 1, "  0%");
      };
  }
}

void pulseCounter1(){
  pulseCount1++;
}

void pulseCounter2(){
  pulseCount2++;
}
